// Logisim project BitBinaryDisplay.circ as structural Verilog: 2 circuits, main circuit twoBitDisplay
module twoBitDisplay (
  input  in_1,
  input  in_2
);

  wire and_1_out, not_1_out, not_2_out, or_1_out, or_2_out;

  not not_1 (not_1_out, in_1);
  not not_2 (not_2_out, in_2);
  or or_1 (or_1_out, not_2_out, in_1);
  or or_2 (or_2_out, not_1_out, in_2);
  and and_1 (and_1_out, not_1_out, not_2_out);
  _7_Segment_Display u_7_segment_display_1 (
    .g(in_1), .f(and_1_out), .a(or_1_out), .b(1'b1), .e(not_2_out), .d(or_1_out), .c(or_2_out));  // open: dp

  // Notes on the sheet:
  //   A
  //   B
  //   7 Segment Display using 2-Bit binary input
  //   that displays decimal output from 0 - 3
endmodule

module fourBitDisplay (
  input  in_1,
  input  in_2,
  input  in_3,
  input  in_4
);

  wire nand_1_out, nand_2_out, nand_3_out, nand_4_out, nand_5_out, nand_6_out, nand_7_out, nand_8_out,
       nand_9_out, nand_10_out, nand_11_out, nand_12_out, nand_13_out, nand_14_out, nand_15_out, nand_16_out,
       nor_1_out, not_1_out, not_2_out, not_3_out, not_4_out;

  not not_1 (not_1_out, in_1);
  not not_2 (not_2_out, in_2);
  not not_3 (not_3_out, in_3);
  not not_4 (not_4_out, in_4);
  nand nand_1 (nand_1_out, in_2, not_3_out, not_4_out);
  nand nand_2 (nand_2_out, not_1_out, not_2_out, not_3_out, in_4);
  nand nand_3 (nand_3_out, in_2, not_3_out, in_4);
  nand nand_4 (nand_4_out, in_2, in_3, not_4_out);
  nor nor_1 (nor_1_out, in_2, not_3_out, in_4);
  nand nand_5 (nand_5_out, in_2, in_3, in_4);
  nand nand_6 (nand_6_out, in_2, not_3_out);
  nand nand_7 (nand_7_out, not_1_out, not_2_out, in_4);
  nand nand_8 (nand_8_out, not_2_out, in_3);
  nand nand_9 (nand_9_out, in_3, in_4);
  nand nand_10 (nand_10_out, not_1_out, not_2_out, not_3_out);
  nand nand_11 (nand_11_out, nand_1_out, nand_2_out);
  nand nand_12 (nand_12_out, nand_3_out, nand_4_out);
  nand nand_13 (nand_13_out, nand_2_out, nand_1_out, nand_5_out);
  nand nand_14 (nand_14_out, nand_7_out, nand_8_out, nand_9_out);
  nand nand_15 (nand_15_out, nand_5_out, nand_10_out);
  nand nand_16 (nand_16_out, nand_6_out, not_4_out);
  _7_Segment_Display #(.active("false")) u_7_segment_display_1 (
    .g(nand_15_out), .f(nand_14_out), .a(nand_11_out), .b(nand_12_out), .e(nand_16_out), .d(nand_13_out),
    .c(nor_1_out));  // open: dp

  // Notes on the sheet:
  //   w
  //   x
  //   y
  //   z
  //   7 Segment Display using 4-Bit binary input
  //   that displays decimal output from 0 - 9
endmodule
